# Fritzing sketch Motion Sensor No Screen (saved by Fritzing 0.9.3b)
breadboards: 1

parts:
  Part1 = Arduino Uno (Rev3) - ICSP
  J1 = Piezo Speaker
  R1 = Resistor [tolerance=±5% resistance=220 package=THT]
  LED1 = LED - 5mm [color="Red (633nm)" package="5 mm [THT]"]
  LED2 = LED - 5mm [color="Blue (525nm)" package="5 mm [THT]"]
  R2 = Resistor [tolerance=±5% resistance=220 package=THT]
  PIR1 = PIR sensor

nets:
  N1: Part1.A0, J1.pin2
  N2: Part1.D9_PWM, LED2.cathode, R2.Pin_0
  N3: Part1.D10_PWM/SS, LED1.cathode
  N4: Part1.D4, PIR1.SIG
  5V: Part1.5V, PIR1.VDD
  GND: Part1.GND, J1.pin1, R1.Pin_1, R2.Pin_1, PIR1.GND
  N5: R1.Pin_0, LED1.anode
